// Logisim project processador.circ as structural Verilog: 5 circuits, main circuit main
module main (
  input  [3:0] in_1,
  input  [3:0] in_2,
  input  [3:0] in_3,
  input  [3:0] in_4,
  input  in_5,
  input  in_6,
  output out_7,
  output out_8,
  output [3:0] out_9,
  output [3:0] out_10
);

  SUB_4 sub_4_1 (.A(in_1), .Overflow(out_7), .B(in_2), .Vem_1(in_5), .out_5(out_9));
  ADD_4 add_4_1 (.A(in_3), .B(in_4), .in_3(in_6), .out_5(out_10), .out_4(out_8));
endmodule

module ADD_1 (
  input  A,
  input  B,
  input  Vem_1,
  output S,
  output Vai_1
);

  wire and_1_out, and_2_out, or_1_out, xor_1_out;

  xor xor_1 (xor_1_out, A, B);
  or or_1 (or_1_out, B, Vem_1);
  and and_1 (and_1_out, or_1_out, A);
  and and_2 (and_2_out, B, Vem_1);
  xor xor_2 (S, xor_1_out, Vem_1);
  or or_2 (Vai_1, and_1_out, and_2_out);
endmodule

module ADD_4 (
  input  [3:0] A,
  input  [3:0] B,
  input  in_3,
  output out_4,
  output [3:0] out_5
);

  wire add_1_1_vai_1, add_1_3_vai_1, add_1_4_vai_1;

  ADD_1 add_1_1 (.A(A[2]), .B(B[2]), .Vem_1(add_1_3_vai_1), .S(out_5[2]), .Vai_1(add_1_1_vai_1));
  ADD_1 add_1_2 (.A(A[3]), .B(B[3]), .Vem_1(add_1_1_vai_1), .S(out_5[3]), .Vai_1(out_4));
  ADD_1 add_1_3 (.A(A[1]), .B(B[1]), .Vem_1(add_1_4_vai_1), .S(out_5[1]), .Vai_1(add_1_3_vai_1));
  ADD_1 add_1_4 (.A(A[0]), .B(B[0]), .Vem_1(in_3), .S(out_5[0]), .Vai_1(add_1_4_vai_1));
endmodule

module SUB_1 (
  input  A,
  input  B,
  input  Vem_1,
  output S,
  output Vai_1
);

  wire and_1_out, and_2_out, or_1_out, xor_1_out;

  xor xor_1 (xor_1_out, A, B);
  or or_1 (or_1_out, B, Vem_1);
  and and_1 (and_1_out, or_1_out, ~A);  // AND_Gate
  and and_2 (and_2_out, B, Vem_1);
  xor xor_2 (S, xor_1_out, Vem_1);
  or or_2 (Vai_1, and_1_out, and_2_out);
endmodule

module SUB_4 (
  input  [3:0] B,
  input  [3:0] A,
  input  Vem_1,
  output Overflow,
  output [3:0] out_5
);

  wire sub_1_1_vai_1, sub_1_3_vai_1, sub_1_4_vai_1;

  SUB_1 sub_1_1 (.A(A[2]), .B(B[2]), .Vem_1(sub_1_3_vai_1), .S(out_5[2]), .Vai_1(sub_1_1_vai_1));
  SUB_1 sub_1_2 (.A(A[3]), .B(B[3]), .Vem_1(sub_1_1_vai_1), .S(out_5[3]), .Vai_1(Overflow));
  SUB_1 sub_1_3 (.A(A[1]), .B(B[1]), .Vem_1(sub_1_4_vai_1), .S(out_5[1]), .Vai_1(sub_1_3_vai_1));
  SUB_1 sub_1_4 (.A(A[0]), .B(B[0]), .Vem_1(Vem_1), .S(out_5[0]), .Vai_1(sub_1_4_vai_1));
endmodule
